// Logisim project Design_of_4bit_Arithmetic_Unit.circ as structural Verilog: 5 circuits, main circuit main
module main (
  input  D0,
  input  D1,
  input  D2,
  input  D3,
  input  S0,
  input  S1,
  input  E,
  output Y
);

  wire and_1_out, and_2_out, and_3_out, and_4_out, not_1_out, not_2_out, not_3_out, not_4_out, not_5_out;

  not not_1 (not_1_out, S0);
  not not_2 (not_2_out, S1);
  not not_3 (not_3_out, not_1_out);
  not not_4 (not_4_out, not_2_out);
  not not_5 (not_5_out, E);
  and and_1 (and_1_out, D0, not_1_out, not_2_out, not_5_out);
  and and_2 (and_2_out, D1, not_1_out, not_4_out, not_5_out);
  and and_3 (and_3_out, D2, not_3_out, not_2_out, not_5_out);
  and and_4 (and_4_out, D3, not_3_out, not_4_out, not_5_out);
  or or_1 (Y, and_1_out, and_2_out, and_3_out, and_4_out);
endmodule

module MUX (
  input  D0,
  input  D1,
  input  D2,
  input  D3,
  input  S0,
  input  S1,
  input  E,
  output Y
);

  wire and_1_out, and_2_out, and_3_out, and_4_out, not_1_out, not_2_out, not_3_out, not_4_out, not_5_out;

  not not_1 (not_1_out, S0);
  not not_2 (not_2_out, not_1_out);
  not not_3 (not_3_out, S1);
  not not_4 (not_4_out, not_3_out);
  not not_5 (not_5_out, E);
  and and_1 (and_1_out, D0, not_1_out, not_3_out, not_5_out);
  and and_2 (and_2_out, D1, not_1_out, not_4_out, not_5_out);
  and and_3 (and_3_out, D2, not_2_out, not_3_out, not_5_out);
  and and_4 (and_4_out, D3, not_2_out, not_4_out, not_5_out);
  or or_1 (Y, and_1_out, and_2_out, and_3_out, and_4_out);
endmodule

module NOT (
  input  in_1,
  input  in_2,
  input  in_3,
  input  in_4,
  input  in_5,
  input  in_6,
  input  in_7,
  input  in_8,
  output out_9,
  output out_10,
  output out_11,
  output out_12,
  output out_13,
  output out_14
);

  not not_1 (out_9, in_1);
  not not_2 (out_10, in_2);
  not not_3 (out_11, in_3);
  not not_4 (out_12, in_4);
  not not_5 (out_13, in_5);
  not not_6 (out_14, in_6);
endmodule

module Adder (
  input  A0,
  input  B0,
  input  C0,
  input  A1,
  input  B1,
  input  A2,
  input  B2,
  input  A3,
  input  B3,
  output D0,
  output D1,
  output D2,
  output D3,
  output C_out
);

  wire and_1_out, and_2_out, and_3_out, and_4_out, and_5_out, and_6_out, and_7_out, and_8_out, xor_1_out,
       xor_2_out, xor_3_out, xor_4_out, xor_6_out, xor_8_out, xor_10_out;

  xor xor_1 (xor_1_out, A3, B3);
  xor xor_2 (xor_2_out, A0, B0);
  and and_1 (and_1_out, A0, B0);
  xor xor_3 (xor_3_out, A1, B1);
  and and_2 (and_2_out, A1, B1);
  xor xor_4 (xor_4_out, A2, B2);
  and and_3 (and_3_out, A2, B2);
  and and_4 (and_4_out, xor_1_out, xor_10_out);
  and and_5 (and_5_out, A3, B3);
  and and_6 (and_6_out, xor_2_out, C0);
  and and_7 (and_7_out, xor_3_out, xor_6_out);
  and and_8 (and_8_out, xor_4_out, xor_8_out);
  xor xor_5 (D0, xor_2_out, C0);
  xor xor_6 (xor_6_out, and_6_out, and_1_out);
  xor xor_7 (D1, xor_3_out, xor_6_out);
  xor xor_8 (xor_8_out, and_7_out, and_2_out);
  xor xor_9 (D2, xor_4_out, xor_8_out);
  xor xor_10 (xor_10_out, and_8_out, and_3_out);
  xor xor_11 (D3, xor_1_out, xor_10_out);
  xor xor_12 (C_out, and_4_out, and_5_out);

  // Notes on the sheet:
  //   C1
  //   C2
  //   C3
endmodule

module Arithmetic_Unit_4bit (
  input  C_in,
  input  S0,
  input  in_3,
  input  S1,
  input  A0,
  input  B0,
  input  A1,
  input  B1,
  input  A2,
  input  B2,
  input  A3,
  input  B3,
  input  in_13,
  output D3,
  output D2,
  output D1,
  output D0,
  output C_out
);

  wire main_1_y, mux_1_y, mux_2_y, mux_3_y, not_1_out_9, not_1_out_10, not_1_out_11, not_1_out_12, not_2_out;

  NOT not_1 (
    .out_9(not_1_out_9), .out_10(not_1_out_10), .out_11(not_1_out_11), .out_12(not_1_out_12), .in_1(B0),
    .in_2(B1), .in_3(B2), .in_4(B3));  // open: out_13, out_14, in_5, in_6, in_7, in_8
  not not_2 (not_2_out, in_13);
  MUX mux_1 (.Y(mux_1_y), .S0(S0), .S1(S1), .E(in_3), .D0(B0), .D1(not_1_out_9), .D2(in_13), .D3(not_2_out));
  MUX mux_2 (.Y(mux_2_y), .S0(S0), .S1(S1), .E(in_3), .D0(B1), .D1(not_1_out_10), .D2(in_13), .D3(not_2_out));
  MUX mux_3 (.Y(mux_3_y), .S0(S0), .S1(S1), .E(in_3), .D0(B2), .D1(not_1_out_11), .D2(in_13), .D3(not_2_out));
  main main_1 (.Y(main_1_y), .S0(S0), .S1(S1), .E(in_3), .D1(not_1_out_12), .D2(in_13), .D3(not_2_out), .D0(B3));
  Adder adder_1 (
    .D3(D3), .C_out(C_out), .D2(D2), .D1(D1), .D0(D0), .A0(A0), .B0(mux_1_y), .C0(C_in), .A3(A3),
    .B3(main_1_y), .A2(A2), .B2(mux_3_y), .A1(A1), .B1(mux_2_y));
endmodule
