// Logisim project Design_of_4bit_Logic_Unit.circ as structural Verilog: 7 circuits, main circuit main
module main (
  input  in_1,
  input  in_2,
  input  in_3,
  input  in_4,
  input  in_5,
  input  in_6,
  input  in_7,
  input  in_8,
  input  in_9,
  input  in_10,
  output out_11,
  output out_12,
  output out_13,
  output out_14
);

  and and_1 (out_11, in_1, in_2);
  and and_2 (out_12, in_3, in_4);
  and and_3 (out_13, in_5, in_6);
  and and_4 (out_14, in_7, in_8);
endmodule

module AND_IC (
  input  in_1,
  input  in_2,
  input  in_3,
  input  in_4,
  input  in_5,
  input  in_6,
  input  in_7,
  input  in_8,
  input  in_9,
  input  in_10,
  output out_11,
  output out_12,
  output out_13,
  output out_14
);

  and and_1 (out_11, in_1, in_2);
  and and_2 (out_12, in_3, in_4);
  and and_3 (out_13, in_5, in_6);
  and and_4 (out_14, in_7, in_8);
endmodule

module OR_IC (
  input  in_1,
  input  in_2,
  input  in_3,
  input  in_4,
  input  in_5,
  input  in_6,
  input  in_7,
  input  in_8,
  input  in_9,
  input  in_10,
  output out_11,
  output out_12,
  output out_13,
  output out_14
);

  or or_1 (out_11, in_1, in_2);
  or or_2 (out_12, in_3, in_4);
  or or_3 (out_13, in_5, in_6);
  or or_4 (out_14, in_7, in_8);
endmodule

module XOR_IC (
  input  in_1,
  input  in_2,
  input  in_3,
  input  in_4,
  input  in_5,
  input  in_6,
  input  in_7,
  input  in_8,
  input  in_9,
  input  in_10,
  output out_11,
  output out_12,
  output out_13,
  output out_14
);

  xor xor_1 (out_11, in_1, in_2);
  xor xor_2 (out_12, in_3, in_4);
  xor xor_3 (out_13, in_5, in_6);
  xor xor_4 (out_14, in_7, in_8);
endmodule

module NOT_IC (
  input  in_1,
  input  in_2,
  input  in_3,
  input  in_4,
  input  in_5,
  input  in_6,
  input  in_7,
  input  in_8,
  output out_9,
  output out_10,
  output out_11,
  output out_12,
  output out_13,
  output out_14
);

  not not_1 (out_9, in_1);
  not not_2 (out_10, in_2);
  not not_3 (out_11, in_3);
  not not_4 (out_12, in_4);
  not not_5 (out_13, in_5);
  not not_6 (out_14, in_6);
endmodule

module MUX_IC (
  input  D0,
  input  D1,
  input  D2,
  input  D3,
  input  S0,
  input  S0_2,
  input  E,
  output out_8
);

  wire and_1_out, and_2_out, and_3_out, and_4_out, not_1_out, not_2_out, not_3_out, not_4_out, not_5_out;

  not not_1 (not_1_out, S0);
  not not_2 (not_2_out, not_1_out);
  not not_3 (not_3_out, S0_2);
  not not_4 (not_4_out, not_3_out);
  not not_5 (not_5_out, E);
  and and_1 (and_1_out, D0, not_1_out, not_3_out, not_5_out);
  and and_2 (and_2_out, D1, not_1_out, not_4_out, not_5_out);
  and and_3 (and_3_out, D2, not_2_out, not_3_out, not_5_out);
  and and_4 (and_4_out, D3, not_2_out, not_4_out, not_5_out);
  or or_1 (out_8, and_1_out, and_2_out, and_3_out, and_4_out);
endmodule

module Logic_Unit_4bit (
  input  A1,
  input  B1,
  input  in_3,
  input  A2,
  input  B2,
  input  S1,
  input  S2,
  output out_8,
  output out_9
);

  wire and_ic_1_out_11, and_ic_2_out_11, not_ic_1_out_9, not_ic_2_out_9, or_ic_1_out_11, or_ic_2_out_11,
       xor_ic_1_out_11, xor_ic_2_out_11;

  AND_IC and_ic_1 (
    .out_11(and_ic_1_out_11), .in_1(B1), .in_2(A1));  // open: out_12, out_13, out_14, in_3, in_4, in_5, in_6, in_7, in_8, in_9, in_10
  OR_IC or_ic_1 (
    .out_11(or_ic_1_out_11), .in_1(B1), .in_2(A1));  // open: out_12, out_13, out_14, in_3, in_4, in_5, in_6, in_7, in_8, in_9, in_10
  AND_IC and_ic_2 (
    .out_11(and_ic_2_out_11), .in_1(B2), .in_2(A2));  // open: out_12, out_13, out_14, in_3, in_4, in_5, in_6, in_7, in_8, in_9, in_10
  OR_IC or_ic_2 (
    .out_11(or_ic_2_out_11), .in_1(B2), .in_2(A2));  // open: out_12, out_13, out_14, in_3, in_4, in_5, in_6, in_7, in_8, in_9, in_10
  XOR_IC xor_ic_1 (
    .out_11(xor_ic_1_out_11), .in_1(B1), .in_2(A1));  // open: out_12, out_13, out_14, in_3, in_4, in_5, in_6, in_7, in_8, in_9, in_10
  NOT_IC not_ic_1 (
    .out_9(not_ic_1_out_9), .in_1(B1));  // open: out_10, out_11, out_12, out_13, out_14, in_2, in_3, in_4, in_5, in_6, in_7, in_8
  XOR_IC xor_ic_2 (
    .out_11(xor_ic_2_out_11), .in_1(B2), .in_2(A2));  // open: out_12, out_13, out_14, in_3, in_4, in_5, in_6, in_7, in_8, in_9, in_10
  NOT_IC not_ic_2 (
    .out_9(not_ic_2_out_9), .in_1(B2));  // open: out_10, out_11, out_12, out_13, out_14, in_2, in_3, in_4, in_5, in_6, in_7, in_8
  MUX_IC mux_ic_1 (
    .out_8(out_8), .D0(and_ic_1_out_11), .D1(or_ic_1_out_11), .D2(xor_ic_1_out_11), .D3(not_ic_1_out_9),
    .S0(S1), .S0_2(S2), .E(in_3));
  MUX_IC mux_ic_2 (
    .out_8(out_9), .D0(and_ic_2_out_11), .D1(or_ic_2_out_11), .D2(xor_ic_2_out_11), .D3(not_ic_2_out_9),
    .S0(S1), .S0_2(S2), .E(in_3));
endmodule
