// Logisim project Design_of_4bit_Multiplier.circ as structural Verilog: 6 circuits, main circuit main
module main (
  input  D0,
  input  D1,
  input  D2,
  input  D3,
  input  S0,
  input  S1,
  input  E,
  output Y
);

  wire and_1_out, and_2_out, and_3_out, and_4_out, not_1_out, not_2_out, not_3_out, not_4_out, not_5_out;

  not not_1 (not_1_out, S0);
  not not_2 (not_2_out, S1);
  not not_3 (not_3_out, not_1_out);
  not not_4 (not_4_out, not_2_out);
  not not_5 (not_5_out, E);
  and and_1 (and_1_out, D0, not_1_out, not_2_out, not_5_out);
  and and_2 (and_2_out, D1, not_1_out, not_4_out, not_5_out);
  and and_3 (and_3_out, D2, not_3_out, not_2_out, not_5_out);
  and and_4 (and_4_out, D3, not_3_out, not_4_out, not_5_out);
  or or_1 (Y, and_1_out, and_2_out, and_3_out, and_4_out);
endmodule

module MUX (
  input  D0,
  input  D1,
  input  D2,
  input  D3,
  input  S0,
  input  S1,
  input  E,
  output Y
);

  wire and_1_out, and_2_out, and_3_out, and_4_out, not_1_out, not_2_out, not_3_out, not_4_out, not_5_out;

  not not_1 (not_1_out, S0);
  not not_2 (not_2_out, not_1_out);
  not not_3 (not_3_out, S1);
  not not_4 (not_4_out, not_3_out);
  not not_5 (not_5_out, E);
  and and_1 (and_1_out, D0, not_1_out, not_3_out, not_5_out);
  and and_2 (and_2_out, D1, not_1_out, not_4_out, not_5_out);
  and and_3 (and_3_out, D2, not_2_out, not_3_out, not_5_out);
  and and_4 (and_4_out, D3, not_2_out, not_4_out, not_5_out);
  or or_1 (Y, and_1_out, and_2_out, and_3_out, and_4_out);
endmodule

module NOT (
  input  in_1,
  input  in_2,
  input  in_3,
  input  in_4,
  input  in_5,
  input  in_6,
  input  in_7,
  input  in_8,
  output out_9,
  output out_10,
  output out_11,
  output out_12,
  output out_13,
  output out_14
);

  not not_1 (out_9, in_1);
  not not_2 (out_10, in_2);
  not not_3 (out_11, in_3);
  not not_4 (out_12, in_4);
  not not_5 (out_13, in_5);
  not not_6 (out_14, in_6);
endmodule

module Adder_4bit (
  input  A0,
  input  B0,
  input  C0,
  input  A1,
  input  B1,
  input  A2,
  input  B2,
  input  A3,
  input  B3,
  output D0,
  output D1,
  output D2,
  output D3,
  output C_out
);

  wire and_1_out, and_2_out, and_3_out, and_4_out, and_5_out, and_6_out, and_7_out, and_8_out, xor_1_out,
       xor_2_out, xor_3_out, xor_4_out, xor_7_out, xor_9_out, xor_12_out;

  xor xor_1 (xor_1_out, A0, B0);
  and and_1 (and_1_out, A0, B0);
  xor xor_2 (xor_2_out, A1, B1);
  and and_2 (and_2_out, A1, B1);
  xor xor_3 (xor_3_out, A2, B2);
  and and_3 (and_3_out, A2, B2);
  xor xor_4 (xor_4_out, A3, B3);
  and and_4 (and_4_out, A3, B3);
  and and_5 (and_5_out, xor_1_out, C0);
  and and_6 (and_6_out, xor_2_out, xor_12_out);
  and and_7 (and_7_out, xor_3_out, xor_7_out);
  and and_8 (and_8_out, xor_4_out, xor_9_out);
  xor xor_5 (D0, xor_1_out, C0);
  xor xor_6 (D1, xor_2_out, xor_12_out);
  xor xor_7 (xor_7_out, and_6_out, and_2_out);
  xor xor_8 (D2, xor_3_out, xor_7_out);
  xor xor_9 (xor_9_out, and_7_out, and_3_out);
  xor xor_10 (D3, xor_4_out, xor_9_out);
  xor xor_11 (C_out, and_8_out, and_4_out);
  xor xor_12 (xor_12_out, and_5_out, and_1_out);

  // Notes on the sheet:
  //   C1
  //   C2
  //   C3
endmodule

module AND_IC (
  input  in_1,
  input  in_2,
  input  in_3,
  input  in_4,
  input  in_5,
  input  in_6,
  input  in_7,
  input  in_8,
  input  in_9,
  input  in_10,
  output out_11,
  output out_12,
  output out_13,
  output out_14
);

  and and_1 (out_11, in_1, in_2);
  and and_2 (out_12, in_3, in_4);
  and and_3 (out_13, in_5, in_6);
  and and_4 (out_14, in_7, in_8);
endmodule

module Multiplier_4bit (
  input  B4,
  input  B3,
  input  B2,
  input  B1,
  input  A4,
  input  A3,
  input  A2,
  input  A1,
  input  in_9
);

  wire adder_4bit_1_c_out, adder_4bit_1_d0, adder_4bit_1_d1, adder_4bit_1_d2, adder_4bit_1_d3,
       adder_4bit_2_c_out, adder_4bit_2_d0, adder_4bit_2_d1, adder_4bit_2_d2, adder_4bit_2_d3,
       adder_4bit_3_c_out, adder_4bit_3_d0, adder_4bit_3_d1, adder_4bit_3_d2, adder_4bit_3_d3,
       and_ic_1_out_11, and_ic_1_out_12, and_ic_1_out_13, and_ic_1_out_14, and_ic_2_out_11, and_ic_2_out_12,
       and_ic_2_out_13, and_ic_2_out_14, and_ic_3_out_11, and_ic_3_out_12, and_ic_3_out_13, and_ic_3_out_14,
       and_ic_4_out_11, and_ic_4_out_12, and_ic_4_out_13, and_ic_4_out_14;

  Adder_4bit adder_4bit_1 (
    .D3(adder_4bit_1_d3), .C_out(adder_4bit_1_c_out), .D2(adder_4bit_1_d2), .D1(adder_4bit_1_d1),
    .D0(adder_4bit_1_d0), .A3(in_9), .B3(and_ic_2_out_14), .B2(and_ic_2_out_13), .A2(and_ic_1_out_14),
    .A1(and_ic_1_out_13), .B1(and_ic_2_out_12), .A0(and_ic_1_out_12), .B0(and_ic_2_out_11), .C0(in_9));
  AND_IC and_ic_1 (
    .out_11(and_ic_1_out_11), .out_12(and_ic_1_out_12), .out_13(and_ic_1_out_13), .out_14(and_ic_1_out_14),
    .in_1(B1), .in_2(A1), .in_3(B2), .in_4(A1), .in_5(B3), .in_6(A1), .in_7(B4), .in_8(A1));  // open: in_9, in_10
  AND_IC and_ic_2 (
    .out_11(and_ic_2_out_11), .out_12(and_ic_2_out_12), .out_13(and_ic_2_out_13), .out_14(and_ic_2_out_14),
    .in_1(B1), .in_2(A2), .in_3(B2), .in_4(A2), .in_5(B3), .in_6(A2), .in_7(B4), .in_8(A2));  // open: in_9, in_10
  AND_IC and_ic_3 (
    .out_11(and_ic_3_out_11), .out_12(and_ic_3_out_12), .out_13(and_ic_3_out_13), .out_14(and_ic_3_out_14),
    .in_1(B1), .in_2(A3), .in_3(B2), .in_4(A3), .in_5(B3), .in_6(A3), .in_7(B4), .in_8(A3));  // open: in_9, in_10
  AND_IC and_ic_4 (
    .out_11(and_ic_4_out_11), .out_12(and_ic_4_out_12), .out_13(and_ic_4_out_13), .out_14(and_ic_4_out_14),
    .in_1(B1), .in_2(A4), .in_3(B2), .in_4(A4), .in_5(B3), .in_6(A4), .in_7(B4), .in_8(A4));  // open: in_9, in_10
  Adder_4bit adder_4bit_2 (
    .D3(adder_4bit_2_d3), .C_out(adder_4bit_2_c_out), .D2(adder_4bit_2_d2), .D1(adder_4bit_2_d1),
    .D0(adder_4bit_2_d0), .A3(adder_4bit_3_c_out), .B3(and_ic_4_out_14), .B2(and_ic_4_out_13),
    .A2(adder_4bit_3_d3), .A1(adder_4bit_3_d2), .B1(and_ic_4_out_12), .A0(adder_4bit_3_d1),
    .B0(and_ic_4_out_11), .C0(in_9));
  Adder_4bit adder_4bit_3 (
    .D3(adder_4bit_3_d3), .C_out(adder_4bit_3_c_out), .D2(adder_4bit_3_d2), .D1(adder_4bit_3_d1),
    .D0(adder_4bit_3_d0), .A3(adder_4bit_1_c_out), .B3(and_ic_3_out_14), .B2(and_ic_3_out_13),
    .A2(adder_4bit_1_d3), .A1(adder_4bit_1_d2), .B1(and_ic_3_out_12), .A0(adder_4bit_1_d1),
    .B0(and_ic_3_out_11), .C0(in_9));
  // Probe on adder_4bit_2_c_out
  // Probe on adder_4bit_2_d3
  // Probe on adder_4bit_2_d2
  // Probe on adder_4bit_2_d1
  // Probe on adder_4bit_2_d0
  // Probe on adder_4bit_3_d0
  // Probe on adder_4bit_1_d0
  // Probe on and_ic_1_out_11

  // Notes on the sheet:
  //   S8
  //   S6
  //   S7
  //   S4
  //   S5
  //   S3
  //   S2
  //   S1
endmodule
