// Logisim project Habibur_Rahaman_Fahim_1911753642_lab_7_modified.circ as structural Verilog
module main (
  input  [15:0] in_1,
  input  Clock,
  input  [3:0] Read_Register_1,
  input  [3:0] Read_Resgister_2,
  input  Write_Enabler,
  input  [3:0] Write_Register
);

  wire demultiplexer_1_out0, demultiplexer_1_out1, demultiplexer_1_out2, demultiplexer_1_out3,
       demultiplexer_1_out4, demultiplexer_1_out5, demultiplexer_1_out6, demultiplexer_1_out7,
       demultiplexer_1_out8, demultiplexer_1_out9, demultiplexer_1_out10, demultiplexer_1_out11,
       demultiplexer_1_out12, demultiplexer_1_out13, demultiplexer_1_out14, demultiplexer_1_out15;
  wire [15:0] multiplexer_1_out, multiplexer_2_out, R0_q, R15_q, register_1_q, register_2_q, register_3_q,
       register_4_q, register_5_q, register_6_q, register_7_q, register_8_q, register_9_q, register_10_q,
       register_11_q, register_12_q, register_13_q, register_14_q;

  Demultiplexer #(.select(4)) demultiplexer_1 (
    .out0(demultiplexer_1_out0), .out1(demultiplexer_1_out1), .out2(demultiplexer_1_out2),
    .out3(demultiplexer_1_out3), .out4(demultiplexer_1_out4), .out5(demultiplexer_1_out5),
    .out6(demultiplexer_1_out6), .out7(demultiplexer_1_out7), .out8(demultiplexer_1_out8),
    .out9(demultiplexer_1_out9), .out10(demultiplexer_1_out10), .out11(demultiplexer_1_out11),
    .out12(demultiplexer_1_out12), .out13(demultiplexer_1_out13), .out14(demultiplexer_1_out14),
    .out15(demultiplexer_1_out15), .in(Write_Enabler), .sel(Write_Register));
  Register #(.width(16)) R0 (.D(in_1), .en(demultiplexer_1_out0), .Q(R0_q), .clk(Clock));  // open: clr
  Register #(.width(16)) register_1 (.D(in_1), .en(demultiplexer_1_out1), .Q(register_1_q), .clk(Clock));  // open: clr
  Register #(.width(16)) register_2 (.D(in_1), .en(demultiplexer_1_out2), .Q(register_2_q), .clk(Clock));  // open: clr
  Register #(.width(16)) register_3 (.D(in_1), .en(demultiplexer_1_out3), .Q(register_3_q), .clk(Clock));  // open: clr
  Register #(.width(16)) register_4 (.D(in_1), .en(demultiplexer_1_out4), .Q(register_4_q), .clk(Clock));  // open: clr
  Register #(.width(16)) register_5 (.D(in_1), .en(demultiplexer_1_out5), .Q(register_5_q), .clk(Clock));  // open: clr
  Register #(.width(16)) register_6 (.D(in_1), .en(demultiplexer_1_out6), .Q(register_6_q), .clk(Clock));  // open: clr
  Register #(.width(16)) register_7 (.D(in_1), .en(demultiplexer_1_out7), .Q(register_7_q), .clk(Clock));  // open: clr
  Register #(.width(16)) register_8 (.D(in_1), .en(demultiplexer_1_out8), .Q(register_8_q), .clk(Clock));  // open: clr
  Register #(.width(16)) register_9 (.D(in_1), .en(demultiplexer_1_out9), .Q(register_9_q), .clk(Clock));  // open: clr
  Register #(.width(16)) register_10 (
    .D(in_1), .en(demultiplexer_1_out10), .Q(register_10_q), .clk(Clock));  // open: clr
  Register #(.width(16)) register_11 (
    .D(in_1), .en(demultiplexer_1_out11), .Q(register_11_q), .clk(Clock));  // open: clr
  Register #(.width(16)) register_12 (
    .D(in_1), .en(demultiplexer_1_out12), .Q(register_12_q), .clk(Clock));  // open: clr
  Register #(.width(16)) register_13 (
    .D(in_1), .en(demultiplexer_1_out13), .Q(register_13_q), .clk(Clock));  // open: clr
  Register #(.width(16)) register_14 (
    .D(in_1), .en(demultiplexer_1_out14), .Q(register_14_q), .clk(Clock));  // open: clr
  Register #(.width(16)) R15 (.D(in_1), .en(demultiplexer_1_out15), .Q(R15_q), .clk(Clock));  // open: clr
  Multiplexer #(.select(4), .width(16)) multiplexer_1 (
    .in0(R0_q), .in1(register_1_q), .in2(register_2_q), .in3(register_3_q), .in4(register_4_q),
    .in5(register_5_q), .in6(register_6_q), .in7(register_7_q), .in8(register_8_q), .in9(register_9_q),
    .in10(register_10_q), .in11(register_11_q), .in12(register_12_q), .in13(register_13_q),
    .in14(register_14_q), .in15(R15_q), .out(multiplexer_1_out), .sel(Read_Register_1));
  Multiplexer #(.select(4), .width(16)) multiplexer_2 (
    .in0(R0_q), .in1(register_1_q), .in2(register_2_q), .in3(register_3_q), .in4(register_4_q),
    .in5(register_5_q), .in6(register_6_q), .in7(register_7_q), .in8(register_8_q), .in9(register_9_q),
    .in10(register_10_q), .in11(register_11_q), .in12(register_12_q), .in13(register_13_q),
    .in14(register_14_q), .in15(R15_q), .out(multiplexer_2_out), .sel(Read_Resgister_2));
  // Probe on multiplexer_1_out
  // Probe on multiplexer_2_out

  // Notes on the sheet:
  //   Write Data
  //   Read Data 1
  //   Read Data 2
endmodule

module Register_Circuit (
  input  [15:0] in_1,
  input  Clock,
  input  [3:0] Write_Register,
  input  [3:0] Read_Register_1,
  input  [3:0] Read_Resgister_2,
  input  Write_Enabler,
  output [15:0] out_7,
  output [15:0] out_8
);

  wire and_1_out, and_2_out, and_3_out, and_4_out, and_5_out, and_6_out, and_7_out, and_8_out, and_9_out,
       and_10_out, and_11_out, and_12_out, and_13_out, and_14_out, and_15_out, and_16_out, decoder_1_out0,
       decoder_1_out1, decoder_1_out2, decoder_1_out3, decoder_1_out4, decoder_1_out5, decoder_1_out6,
       decoder_1_out7, decoder_1_out8, decoder_1_out9, decoder_1_out10, decoder_1_out11, decoder_1_out12,
       decoder_1_out13, decoder_1_out14, decoder_1_out15;
  wire [15:0] R0_q, R15_q, register_1_q, register_2_q, register_3_q, register_4_q, register_5_q,
       register_6_q, register_7_q, register_8_q, register_9_q, register_10_q, register_11_q, register_12_q,
       register_13_q, register_14_q;

  Decoder #(.select(4)) decoder_1 (
    .out0(decoder_1_out0), .out1(decoder_1_out1), .out2(decoder_1_out2), .out3(decoder_1_out3),
    .out4(decoder_1_out4), .out5(decoder_1_out5), .out6(decoder_1_out6), .out7(decoder_1_out7),
    .out8(decoder_1_out8), .out9(decoder_1_out9), .out10(decoder_1_out10), .out11(decoder_1_out11),
    .out12(decoder_1_out12), .out13(decoder_1_out13), .out14(decoder_1_out14), .out15(decoder_1_out15),
    .sel(Write_Register));  // open: en
  and and_1 (and_1_out, decoder_1_out0, Write_Enabler);
  and and_2 (and_2_out, decoder_1_out1, Write_Enabler);
  and and_3 (and_3_out, decoder_1_out2, Write_Enabler);
  and and_4 (and_4_out, decoder_1_out3, Write_Enabler);
  and and_5 (and_5_out, decoder_1_out4, Write_Enabler);
  and and_6 (and_6_out, decoder_1_out5, Write_Enabler);
  and and_7 (and_7_out, decoder_1_out6, Write_Enabler);
  and and_8 (and_8_out, decoder_1_out7, Write_Enabler);
  and and_9 (and_9_out, decoder_1_out8, Write_Enabler);
  and and_10 (and_10_out, decoder_1_out9, Write_Enabler);
  and and_11 (and_11_out, decoder_1_out10, Write_Enabler);
  and and_12 (and_12_out, decoder_1_out11, Write_Enabler);
  and and_13 (and_13_out, decoder_1_out12, Write_Enabler);
  and and_14 (and_14_out, decoder_1_out13, Write_Enabler);
  and and_15 (and_15_out, decoder_1_out14, Write_Enabler);
  and and_16 (and_16_out, decoder_1_out15, Write_Enabler);
  Register #(.width(16)) R0 (.D(in_1), .en(and_1_out), .Q(R0_q), .clk(Clock));  // open: clr
  Register #(.width(16)) register_1 (.D(in_1), .en(and_2_out), .Q(register_1_q), .clk(Clock));  // open: clr
  Register #(.width(16)) register_2 (.D(in_1), .en(and_3_out), .Q(register_2_q), .clk(Clock));  // open: clr
  Register #(.width(16)) register_3 (.D(in_1), .en(and_4_out), .Q(register_3_q), .clk(Clock));  // open: clr
  Register #(.width(16)) register_4 (.D(in_1), .en(and_5_out), .Q(register_4_q), .clk(Clock));  // open: clr
  Register #(.width(16)) register_5 (.D(in_1), .en(and_6_out), .Q(register_5_q), .clk(Clock));  // open: clr
  Register #(.width(16)) register_6 (.D(in_1), .en(and_7_out), .Q(register_6_q), .clk(Clock));  // open: clr
  Register #(.width(16)) register_7 (.D(in_1), .en(and_8_out), .Q(register_7_q), .clk(Clock));  // open: clr
  Register #(.width(16)) register_8 (.D(in_1), .en(and_9_out), .Q(register_8_q), .clk(Clock));  // open: clr
  Register #(.width(16)) register_9 (.D(in_1), .en(and_10_out), .Q(register_9_q), .clk(Clock));  // open: clr
  Register #(.width(16)) register_10 (.D(in_1), .en(and_11_out), .Q(register_10_q), .clk(Clock));  // open: clr
  Register #(.width(16)) register_11 (.D(in_1), .en(and_12_out), .Q(register_11_q), .clk(Clock));  // open: clr
  Register #(.width(16)) register_12 (.D(in_1), .en(and_13_out), .Q(register_12_q), .clk(Clock));  // open: clr
  Register #(.width(16)) register_13 (.D(in_1), .en(and_14_out), .Q(register_13_q), .clk(Clock));  // open: clr
  Register #(.width(16)) register_14 (.D(in_1), .en(and_15_out), .Q(register_14_q), .clk(Clock));  // open: clr
  Register #(.width(16)) R15 (.D(in_1), .en(and_16_out), .Q(R15_q), .clk(Clock));  // open: clr
  Multiplexer #(.select(4), .width(16)) multiplexer_1 (
    .in0(R0_q), .in1(register_1_q), .in2(register_2_q), .in3(register_3_q), .in4(register_4_q),
    .in5(register_5_q), .in6(register_6_q), .in7(register_7_q), .in8(register_8_q), .in9(register_9_q),
    .in10(register_10_q), .in11(register_11_q), .in12(register_12_q), .in13(register_13_q),
    .in14(register_14_q), .in15(R15_q), .out(out_7), .sel(Read_Register_1));
  Multiplexer #(.select(4), .width(16)) multiplexer_2 (
    .in0(R0_q), .in1(register_1_q), .in2(register_2_q), .in3(register_3_q), .in4(register_4_q),
    .in5(register_5_q), .in6(register_6_q), .in7(register_7_q), .in8(register_8_q), .in9(register_9_q),
    .in10(register_10_q), .in11(register_11_q), .in12(register_12_q), .in13(register_13_q),
    .in14(register_14_q), .in15(R15_q), .out(out_8), .sel(Read_Resgister_2));

  // Notes on the sheet:
  //   Write Data
  //   Read Data 1
  //   Read Data 2
endmodule

module ALU (
  input  in_1,
  input  in_2,
  input  [15:0] in_3,
  input  [2:0] in_4,
  input  Write_Enable,
  output [3:0] Opcode,
  output [3:0] RS,
  output [3:0] RT,
  output [3:0] Imm,
  output [15:0] out_10,
  output [15:0] out_11,
  output [15:0] out_12
);

  wire clock_1_out;
  wire [15:0] adder_1_out, register_1_q;

  Clock clock_1 (.out(clock_1_out));
  Register #(.width(16)) register_1 (.D(adder_1_out), .Q(register_1_q), .clk(clock_1_out));  // open: en, clr
  ROM #(.addrWidth(16), .dataWidth(16)) rom_1 (.addr(register_1_q), .data({Opcode, RS, RT, Imm}));
  Adder #(.width(16)) adder_1 (.a(register_1_q), .b(16'h1), .out(adder_1_out));  // open: cin, cout
  Register_Circuit register_circuit_1 (
    .out_7(out_10), .Read_Register_1(RS), .in_1(out_12), .Write_Enabler(Write_Enable), .Write_Register(RT),
    .Clock(clock_1_out));  // open: out_8, Read_Resgister_2
  assign out_11 = {{12{1'b0}}, Imm};  // Bit_Extender bit_extender_1
  ALU_Upgraded alu_upgraded_1 (.out_6(out_12), .in_2(out_10), .in_3(out_11), .in_4(in_2), .Cin(in_1), .in_5(in_4));

  // Notes on the sheet:
  //   CLK
  //   contents of rom_1 (hex, n*v repeats v):
  //   4000 239
  //   Write Data
  //   Write Back
  //   Data 1
  //   Data 2
  //   ALU Result
endmodule

module ALU_Upgraded (
  input  Cin,
  input  [15:0] in_2,
  input  [15:0] in_3,
  input  in_4,
  input  [2:0] in_5,
  output [15:0] out_6
);

  wire [15:0] adder_1_out, and_1_out, multiplexer_1_out, nand_1_out, nor_1_out, not_1_out, or_1_out,
       shifter_1_out;

  Multiplexer #(.width(16)) multiplexer_1 (.in0(in_3), .in1(not_1_out), .out(multiplexer_1_out), .sel(in_4));
  assign not_1_out = ~in_3;  // NOT_Gate not_1, 16 bits wide
  Adder #(.width(16)) adder_1 (.a(in_2), .b(multiplexer_1_out), .out(adder_1_out), .cin(Cin));  // open: cout
  assign nor_1_out = ~(in_2 | multiplexer_1_out);  // NOR_Gate nor_1, 16 bits wide
  assign and_1_out = in_2 & multiplexer_1_out;  // AND_Gate and_1, 16 bits wide
  assign or_1_out = in_2 | multiplexer_1_out;  // OR_Gate or_1, 16 bits wide
  assign nand_1_out = ~(in_2 & multiplexer_1_out);  // NAND_Gate nand_1, 16 bits wide
  Shifter #(.width(16)) shifter_1 (.in(in_2), .\dist (multiplexer_1_out[3:0]), .out(shifter_1_out));
  Multiplexer #(.select(3), .width(16)) multiplexer_2 (
    .in0(adder_1_out), .in1(nor_1_out), .in2(and_1_out), .in3(or_1_out), .in4(nand_1_out),
    .in5(shifter_1_out), .out(out_6), .sel(in_5));  // open: in6, in7

  // Notes on the sheet:
  //   A
  //   B
  //   B-Invert
  //   Select bit  operation
  //   Result
endmodule

module I_ALU (
  input  [3:0] Opcode,
  input  in_2,
  input  in_3,
  input  [15:0] in_4,
  input  [2:0] in_5,
  input  Write_Enable,
  output [3:0] RS,
  output [3:0] RT,
  output [3:0] Imm,
  output [15:0] out_10,
  output [15:0] out_11,
  output [15:0] out_12
);

  wire clock_1_out;
  wire [15:0] adder_1_out, register_1_q;

  Clock clock_1 (.out(clock_1_out));
  Register #(.width(16)) register_1 (.D(adder_1_out), .Q(register_1_q), .clk(clock_1_out));  // open: en, clr
  ROM #(.addrWidth(16), .dataWidth(16)) rom_1 (.addr(register_1_q), .data({Opcode, RS, RT, Imm}));
  Adder #(.width(16)) adder_1 (.a(register_1_q), .b(16'h1), .out(adder_1_out));  // open: cin, cout
  Register_Circuit register_circuit_1 (
    .out_7(out_10), .Read_Register_1(RS), .in_1(out_12), .Write_Enabler(Write_Enable), .Write_Register(RT),
    .Clock(clock_1_out));  // open: out_8, Read_Resgister_2
  assign out_11 = {{12{1'b0}}, Imm};  // Bit_Extender bit_extender_1
  ALU_Upgraded alu_upgraded_1 (.out_6(out_12), .in_2(out_10), .in_3(out_11), .in_4(in_3), .Cin(in_2), .in_5(in_5));

  // Notes on the sheet:
  //   CLK
  //   Write Data
  //   Write Back
  //   Data 1
  //   Data 2
  //   ALU Result
endmodule

module Load_ALU (
  input  in_1,
  input  in_2,
  input  [15:0] in_3,
  input  [2:0] in_4,
  input  Write_Enable,
  input  in_6,
  output [3:0] Opcode,
  output [3:0] RS,
  output [3:0] RT,
  output [3:0] Imm,
  output [15:0] out_11,
  output [15:0] out_12,
  output [15:0] out_13
);

  wire clock_1_out;
  wire [15:0] adder_1_out, register_1_q, undriven;

  Clock clock_1 (.out(clock_1_out));
  Clock clock_2 ();  // open: out
  Register #(.width(16)) register_1 (.D(adder_1_out), .Q(register_1_q), .clk(clock_1_out));  // open: en, clr
  ROM #(.addrWidth(16), .dataWidth(16)) rom_1 (.addr(register_1_q), .data({Opcode, RS, RT, Imm}));
  Adder #(.width(16)) adder_1 (.a(register_1_q), .b(16'h1), .out(adder_1_out));  // open: cin, cout
  Register_Circuit register_circuit_1 (
    .out_7(out_11), .Read_Register_1(RS), .in_1(undriven), .Write_Enabler(Write_Enable), .Write_Register(RT),
    .Clock(clock_1_out));  // open: out_8, Read_Resgister_2
  assign out_12 = {{12{1'b0}}, Imm};  // Bit_Extender bit_extender_1
  RAM #(.addrWidth(16), .asyncread("true"), .dataWidth(16)) ram_1 (
    .addr(out_13), .we(in_6));  // open: oe, clk, din, dout
  ALU_Upgraded alu_upgraded_1 (.out_6(out_13), .in_2(out_11), .in_3(out_12), .in_4(in_2), .Cin(in_1), .in_5(in_4));

  // Notes on the sheet:
  //   CLK
  //   contents of rom_1 (hex, n*v repeats v):
  //   5189
  //   Write Data
  //   Write Back
  //   Data 1
  //   Data 2
  //   ALU Result
endmodule

module Store_ALU (
  input  in_1,
  input  in_2,
  input  [15:0] in_3,
  input  [2:0] in_4,
  input  in_5,
  input  in_6,
  output [3:0] Opcode,
  output [3:0] RS,
  output [3:0] RT,
  output [3:0] Imm,
  output [15:0] out_11,
  output [15:0] out_12,
  output [15:0] out_13
);

  wire clock_1_out;
  wire [15:0] adder_1_out, register_1_q, register_circuit_1_out_8;

  Clock clock_1 (.out(clock_1_out));
  Clock clock_2 ();  // open: out
  Register #(.width(16)) register_1 (.D(adder_1_out), .Q(register_1_q), .clk(clock_1_out));  // open: en, clr
  ROM #(.addrWidth(16), .dataWidth(16)) rom_1 (.addr(register_1_q), .data({Opcode, RS, RT, Imm}));
  Adder #(.width(16)) adder_1 (.a(register_1_q), .b(16'h1), .out(adder_1_out));  // open: cin, cout
  Register_Circuit register_circuit_1 (
    .out_7(out_11), .out_8(register_circuit_1_out_8), .Read_Register_1(RS), .Write_Enabler(in_5),
    .Write_Register(RT), .Clock(clock_1_out));  // open: Read_Resgister_2, in_1
  assign out_12 = {{12{1'b0}}, Imm};  // Bit_Extender bit_extender_1
  RAM #(.addrWidth(16), .dataWidth(16), .trigger("high")) ram_1 (
    .addr(out_13), .we(in_6), .din(register_circuit_1_out_8));  // open: oe, dout
  ALU_Upgraded alu_upgraded_1 (.out_6(out_13), .in_2(out_11), .in_3(out_12), .in_4(in_2), .Cin(in_1), .in_5(in_4));

  // Notes on the sheet:
  //   CLK
  //   contents of rom_1 (hex, n*v repeats v):
  //   5189
  //   Write Data
  //   Write Back
  //   Data 1
  //   Data 2
  //   ALU Result
endmodule

module ALL_ALU (
  input  [2:0] in_1,
  input  Write_Enable,
  input  Store_enb,
  input  Load_enb,
  input  Reg_Dst,
  input  ALU_Src,
  input  Sub,
  input  RAM_to_Reg,
  output [3:0] Opcode,
  output [3:0] RS,
  output [3:0] RT,
  output [3:0] Write_Reg___RD,
  output [15:0] out_13,
  output [15:0] out_14,
  output [15:0] out_15,
  output [15:0] out_16
);

  wire clock_1_out;
  wire [3:0] multiplexer_1_out;
  wire [15:0] adder_1_out, alu_upgraded_1_out_6, bit_extender_1_out, ram_1_dout, register_1_q;

  Clock clock_1 (.out(clock_1_out));
  Register #(.width(16)) register_1 (.D(adder_1_out), .Q(register_1_q));  // open: en, clk, clr
  ROM #(.addrWidth(16), .dataWidth(16)) rom_1 (.addr(register_1_q), .data({Opcode, RS, RT, Write_Reg___RD}));
  Adder #(.width(16)) adder_1 (.a(register_1_q), .b(16'h1), .out(adder_1_out));  // open: cin, cout
  Multiplexer #(.width(4)) multiplexer_1 (.in0(Write_Reg___RD), .in1(RT), .out(multiplexer_1_out), .sel(Reg_Dst));
  Register_Circuit register_circuit_1 (
    .out_7(out_13), .out_8(out_16), .Read_Register_1(RS), .Read_Resgister_2(RT), .in_1(out_15),
    .Write_Enabler(Write_Enable), .Write_Register(multiplexer_1_out), .Clock(clock_1_out));
  assign bit_extender_1_out = {{12{1'b0}}, Write_Reg___RD};  // Bit_Extender bit_extender_1
  Multiplexer #(.width(16)) multiplexer_2 (.in0(out_16), .in1(bit_extender_1_out), .out(out_14), .sel(ALU_Src));
  RAM #(.addrWidth(16), .asyncread("true"), .clearpin("true"), .dataWidth(16)) ram_1 (
    .addr(alu_upgraded_1_out_6), .we(Store_enb), .oe(Load_enb), .clk(clock_1_out), .din(out_16),
    .dout(ram_1_dout));  // open: clr
  ALU_Upgraded alu_upgraded_1 (
    .out_6(alu_upgraded_1_out_6), .in_2(out_13), .in_3(out_14), .in_4(Sub), .Cin(Sub), .in_5(in_1));
  Multiplexer #(.width(16)) multiplexer_3 (
    .in0(alu_upgraded_1_out_6), .in1(ram_1_dout), .out(out_15), .sel(RAM_to_Reg));

  // Notes on the sheet:
  //   CLK
  //   contents of rom_1 (hex, n*v repeats v):
  //   4567
  //   Write Back
  //   Jump
  //   Data 1
  //   Data 2
  //   Data for store
  //   ALU Result
endmodule
